// Logisim project 8bitsProcesador.circ as structural Verilog
module ALU (
  input  [7:0] A,
  input  [7:0] B,
  input  [1:0] ALU_Opt,
  output Zero,
  output [7:0] ALU_Respuesta
);

  wire [7:0] adder_1_out, and_1_out, or_1_out, subtractor_1_out;

  Adder adder_1 (.a(A), .b(B), .out(adder_1_out));  // open: cin, cout
  Subtractor subtractor_1 (.a(A), .b(B), .out(subtractor_1_out));  // open: bin, bout
  assign and_1_out = A & B;  // AND_Gate and_1, 8 bits wide
  assign or_1_out = A | B;  // OR_Gate or_1, 8 bits wide
  Multiplexer #(.select(2), .width(8)) multiplexer_1 (
    .in0(adder_1_out), .in1(subtractor_1_out), .in2(and_1_out), .in3(or_1_out), .out(ALU_Respuesta),
    .sel(ALU_Opt));  // open: en
  Comparator comparator_1 (.a({8{1'b0}}), .b(ALU_Respuesta), .eq(Zero));  // open: gt, lt
endmodule

module ALUControl (
  input  [1:0] ALUOp,
  input  [2:0] \Función ,
  output [1:0] \Operación 
);

  wire and_1_out, not_1_out;

  not not_1 (not_1_out, ALUOp[0]);
  and and_1 (and_1_out, not_1_out, ALUOp[1]);
  Multiplexer multiplexer_1 (.in0(ALUOp[0]), .in1(\Función [0]), .out(\Operación [0]), .sel(and_1_out));  // open: en
  Multiplexer multiplexer_2 (.in0(ALUOp[1]), .in1(\Función [1]), .out(\Operación [1]), .sel(and_1_out));  // open: en
endmodule

module UnidadControl (
  input  [2:0] Entrada,
  output RegDst,
  output Branch,
  output MemRead,
  output MemtoReg,
  output [1:0] ALUOp,
  output MemWrite,
  output ALUSrc,
  output RegWrite,
  output Jump
);

  wire not_1_out, not_2_out, not_3_out, not_4_out, not_5_out, not_6_out, not_7_out, not_8_out, not_9_out,
       not_10_out;

  not not_1 (not_1_out, Entrada[0]);
  not not_2 (not_2_out, Entrada[1]);
  not not_3 (not_3_out, Entrada[2]);
  not not_4 (not_4_out, Entrada[1]);
  not not_5 (not_5_out, Entrada[2]);
  not not_6 (not_6_out, Entrada[0]);
  not not_7 (not_7_out, Entrada[2]);
  not not_8 (not_8_out, Entrada[2]);
  not not_9 (not_9_out, Entrada[0]);
  not not_10 (not_10_out, Entrada[1]);
  and R (ALUOp[1], not_1_out, not_2_out, not_3_out);
  and lw (MemRead, Entrada[0], not_4_out, not_5_out);
  and sw (MemWrite, not_6_out, Entrada[1], not_7_out);
  and beq (ALUOp[0], Entrada[0], Entrada[1], not_8_out);
  and j (Jump, not_9_out, not_10_out, Entrada[2]);
  or or_1 (ALUSrc, MemWrite, MemRead);
  or or_2 (RegWrite, MemRead, ALUOp[1]);

  assign Branch = ALUOp[0];
  assign MemtoReg = MemRead;
  assign RegDst = ALUOp[1];
endmodule
